// Logisim project DataPath.circ as structural Verilog: 19 circuits, main circuit Full Adder 1Bit
module Full_Adder_1Bit (
  input  A,
  input  B,
  input  C,
  output S,
  output Carry
);

  wire and_1_out, and_2_out, xor_1_out;

  xor xor_1 (xor_1_out, A, B);
  xor xor_2 (S, xor_1_out, C);
  and and_1 (and_1_out, A, B);
  and and_2 (and_2_out, xor_1_out, C);
  or or_1 (Carry, and_1_out, and_2_out);
endmodule

module Full_Adder (
  input  [3:0] A,
  input  [3:0] B,
  input  Cin,
  output Cout,
  output [3:0] Sub
);

  wire full_adder_1bit_2_carry, full_adder_1bit_3_carry, full_adder_1bit_4_carry, xor_1_out, xor_2_out,
       xor_3_out, xor_4_out;

  // Probe on A
  // Probe on B
  xor xor_1 (xor_1_out, B[3], Cin);
  Full_Adder_1Bit full_adder_1bit_1 (.A(A[3]), .B(xor_1_out), .S(Sub[3]), .C(full_adder_1bit_2_carry), .Carry(Cout));
  xor xor_2 (xor_2_out, B[2], Cin);
  Full_Adder_1Bit full_adder_1bit_2 (
    .A(A[2]), .B(xor_2_out), .S(Sub[2]), .C(full_adder_1bit_3_carry), .Carry(full_adder_1bit_2_carry));
  xor xor_3 (xor_3_out, B[1], Cin);
  Full_Adder_1Bit full_adder_1bit_3 (
    .A(A[1]), .B(xor_3_out), .S(Sub[1]), .C(full_adder_1bit_4_carry), .Carry(full_adder_1bit_3_carry));
  xor xor_4 (xor_4_out, B[0], Cin);
  // Probe on Sub
  Full_Adder_1Bit full_adder_1bit_4 (.A(A[0]), .B(xor_4_out), .S(Sub[0]), .C(Cin), .Carry(full_adder_1bit_4_carry));
endmodule

module SCP (
  input  Reset
);

  wire ALUSrc, Carry_F, CLK, CLK_IF_ID, comparator_1_eq, comparator_2_gt, Extender, Kill, Kill_Ins_D,
       MemRead, MemWrite, Neg_F, not_1_out, not_2_out, Overflow_F, RALUSrc, RALUSrc_EX, RegDes, RMemRead,
       RMemRead_EX, RMemRead_MEM, RMemWrite, RMemWrite_EX, RMemWrite_MEM, RWE, RWE__EX, RWE_EX, RWE_MEM,
       RWE_WB, Stall, WE, Zero_F;
  wire [1:0] FA, FB, FP, PC_Selection, RPC_Selection, RWB, RWB_EX, RWB_MEM, WB;
  wire [2:0] AluOP, AluOp_EX, AluOp_t;
  wire [4:0] multiplexer_2_out, Rd_EX, Rd_MEM, Rd_WB;
  wire [11:0] Imm;
  wire [19:0] NextPC, PC, PCPluse, RS;
  wire [31:0] A_F, A_F_EX, ALU_RES, ALU_RES_MEM, B_F, B_F_EX, B_F_MEM, BusP, BusX, BusY, BusZ, DATA,
       DATA_MEM, DATA_WB, ImmN, ImmN_EX, Instruction, multiplexer_12_out, P_F, pc_t, pcPluse1, pcPluse1_EX,
       pcPluse1_ID, pcPluse1_MEM, R1, R2, R3, R4, R5, R6, R7, R8, R9, R10, R11, R12, R13, R14, R15, R16, R17,
       R18, R19, R20, R21, R22, R23, R24, R25, R26, R27, R28, R29, R30, R31, rom_1_data;
  wire [31:12] Instruction_ID;

  not not_1 (not_1_out, Stall);
  Clock u_CLK (.out(CLK));
  Register #(.width(20)) u_PC (.D(NextPC), .en(not_1_out), .Q(PC), .clk(CLK), .clr(Reset));
  PC_Control pc_control_1 (
    .PC(PC), .OFFSET({Instruction_ID[21:12], Imm}), .PC_Selection(RPC_Selection), .NPC(PCPluse), .Reg(RS),
    .NextPC(NextPC));
  ROM #(.addrWidth(20), .dataWidth(32)) rom_1 (.addr(PC), .data(rom_1_data));  // open: sel
  Adder #(.width(20)) adder_1 (.a(PC), .b(20'h1), .out(PCPluse));  // open: cin, cout
  Multiplexer #(.width(32), .enable("false")) multiplexer_1 (
    .in0(rom_1_data), .in1({32{1'b0}}), .out(Instruction), .sel(Kill));
  not not_2 (not_2_out, Stall);
  and and_1 (CLK_IF_ID, CLK, not_2_out);
  IF_ID if_id_1 (
    .Instruction(Instruction), .PC(pcPluse1), .clk(CLK_IF_ID), .out_4({Instruction_ID, Imm}),
    .out_5(pcPluse1_ID));
  Control_Unit control_unit_1 (
    .Op_Code(Instruction_ID[31:27]), .WBdata(WB), .MemRead(MemRead), .MemWrite(MemWrite),
    .PCSel(PC_Selection), .ALUSrc(ALUSrc), .ExtOp(Extender), .WE(WE), .RegDes(RegDes), .ALUOP(AluOP));
  Multiplexer #(.width(5), .enable("false")) multiplexer_2 (
    .in0(Instruction_ID[21:17]), .in1({5{1'b1}}), .out(multiplexer_2_out), .sel(RegDes));
  Hazarad_Detection hazarad_detection_1 (
    .MEMR(RMemRead_EX), .FA(FA), .FB(FB), .OPCode(Instruction_ID[31:27]), .Stall(Stall), .Kill(Kill), .FP(FP));
  Extender extender_1 (.Imm(Imm), .ImmExtender(ImmN), .EXTSignal(Extender));
  Comparator #(.width(32)) comparator_1 (.a(P_F), .b({32{1'b0}}), .eq(comparator_1_eq));  // open: gt, lt
  Comparator #(.width(5)) comparator_2 (
    .a(Instruction_ID[26:22]), .b({5{1'b0}}), .gt(comparator_2_gt));  // open: eq, lt
  Multiplexer #(.enable("false")) multiplexer_3 (.in0(WE), .in1(1'b0), .out(RWE), .sel(Kill_Ins_D));
  and and_2 (Kill_Ins_D, comparator_1_eq, comparator_2_gt);
  Multiplexer #(.enable("false")) multiplexer_4 (.in0(MemRead), .in1(1'b0), .out(RMemRead), .sel(Kill_Ins_D));
  Multiplexer #(.enable("false")) multiplexer_5 (.in0(MemWrite), .in1(1'b0), .out(RMemWrite), .sel(Kill_Ins_D));
  Multiplexer #(.enable("false")) multiplexer_6 (.in0(ALUSrc), .in1(1'b0), .out(RALUSrc), .sel(Kill_Ins_D));
  Multiplexer #(.width(2), .enable("false")) multiplexer_7 (
    .in0(PC_Selection), .in1(2'b00), .out(RPC_Selection), .sel(Kill_Ins_D));
  Multiplexer #(.width(2), .enable("false")) multiplexer_8 (.in0(WB), .in1(2'b00), .out(RWB), .sel(Kill_Ins_D));
  RFile rfile_1 (
    .RZ(Imm[11:7]), .RY(Instruction_ID[16:12]), .BusX(BusX), .RX(multiplexer_2_out), .Bus_Z(BusZ),
    .Enable(WE), .Bus_Y(BusY), .CLK(CLK), .Reg1(R1), .Reg2(R2), .Reg3(R3), .Reg4(R4), .Reg5(R5), .Reg6(R6),
    .Reg7(R7), .Reg8(R8), .Reg9(R9), .Reg10(R10), .Reg11(R11), .Reg12(R12), .Reg13(R13), .Reg14(R14),
    .Reg15(R15), .Reg16(R16), .Reg17(R17), .Reg18(R18), .Reg19(R31), .Reg20(R30), .Reg21(R29), .Reg22(R28),
    .Reg23(R27), .Reg24(R26), .Reg25(R25), .Reg26(R24), .Reg27(R23), .Reg28(R22), .Reg29(R21), .Reg30(R20),
    .Reg31(R19), .Rp(Instruction_ID[26:22]), .BUSp(BusP), .PC(pc_t));
  Forwarding_Unit forwarding_unit_1 (
    .RS1(Instruction_ID[16:12]), .RD1(Rd_EX), .WE_EX(RWE_EX), .MemRead_MEM(RMemRead_MEM), .RS2(Imm[11:7]),
    .RD2(Rd_MEM), .RD3(Rd_WB), .WE_WB(RWE_WB), .RP(Instruction_ID[26:22]), .FA(FA), .FB(FB), .FP(FP));
  Multiplexer #(.select(2), .width(32), .enable("false")) multiplexer_9 (
    .in0(BusY), .in1(ALU_RES), .in2(DATA_MEM), .in3(DATA_WB), .out(A_F), .sel(FA));
  Multiplexer #(.select(2), .width(32), .enable("false")) multiplexer_10 (
    .in0(BusZ), .in1(ALU_RES), .in2(DATA_MEM), .in3(DATA_WB), .out(B_F), .sel(FB));
  Multiplexer #(.select(2), .width(32), .enable("false")) multiplexer_11 (
    .in0(BusP), .in1(ALU_RES), .in2(DATA_MEM), .in3(DATA_WB), .out(P_F), .sel(FP));
  ID_EX id_ex_1 (
    .SOURCE1(A_F), .in_2(A_F_EX), .SOURCE2(B_F), .in_4(B_F_EX), .IMM(ImmN), .in_6(ImmN_EX),
    .DESTENATION(Instruction_ID[21:17]), .in_12(Rd_EX), .ALUOP(AluOp_t), .out_19(AluOp_EX), .in_18(CLK),
    .Regwrite(RWE), .in_16(RWE__EX), .MEMR(RMemRead), .MEMW(RMemWrite), .out_21(RMemWrite_EX),
    .out_22(RMemRead_EX), .ALUSrc(RALUSrc), .out_20(RALUSrc_EX), .WB(RWB), .out_23(RWB_EX),
    .PC_1(pcPluse1_ID), .in_8(pcPluse1_EX));
  Multiplexer #(.width(32), .enable("false")) multiplexer_12 (
    .in0(B_F_EX), .in1(ImmN_EX), .out(multiplexer_12_out), .sel(RALUSrc_EX));
  ALU alu_1 (
    .A(A_F_EX), .ALU_Operation(AluOp_EX), .VF(Overflow_F), .ZF(Zero_F), .NF(Neg_F), .B(multiplexer_12_out),
    .ALU_Result(ALU_RES), .CF(Carry_F));
  EX_MEM ex_mem_1 (
    .ALU_RES(ALU_RES), .SOURCE2(B_F_EX), .DESTENATION(Rd_EX), .Regwrite(RMemWrite_EX), .MemRd(RMemRead_EX),
    .MemWr(RWE__EX), .in_16(CLK), .out_17(ALU_RES_MEM), .in_3(B_F_MEM), .in_7(Rd_MEM), .in_9(RMemWrite_MEM),
    .in_11(RMemRead_MEM), .in_13(RWE_MEM), .WB_DATA(RWB_EX), .in_15(RWB_MEM), .PC_1(pcPluse1_EX),
    .in_5(pcPluse1_MEM));
  RAM #(.addrWidth(20), .dataWidth(32), .bus("separate")) ram_1 (
    .addr(ALU_RES_MEM[19:0]), .din(B_F_MEM), .data(DATA_MEM), .str(RMemWrite_MEM), .clk(CLK),
    .ld(RMemRead_MEM));  // open: sel, clr
  Multiplexer #(.select(2), .width(32), .enable("false")) multiplexer_13 (
    .in0(ALU_RES_MEM), .in1(DATA_MEM), .in2(pcPluse1_MEM), .in3({32{1'b0}}), .out(DATA), .sel(RWB_MEM));
  MEM_WB mem_wb_1 (
    .DATA(DATA), .DESTENATION(Rd_MEM), .Regwrite(RWE_MEM), .in_7(CLK), .in_2(DATA_WB), .in_4(Rd_WB),
    .in_6(RWE_WB));

  // Other names for the same wires on the sheet: Instruction_ID[11:0] = Imm;
  //   Offset[21:0] = {Instruction_ID[21:12], Imm}; Unuseed[6:0] = Imm[6:0]; Rt[4:0] = Imm[11:7];
  //   Rs_t[4:0] = Instruction_ID[16:12]; Rd[4:0] = Instruction_ID[21:17]; Rp[4:0] = Instruction_ID[26:22];
  //   OpCode[4:0] = Instruction_ID[31:27]

  // Notes on the sheet:
  //   contents of rom_1 (hex, n*v repeats v):
  //   c1003 0 0 c2006 0 0 c3008 0 0 c4002 0 0 c5007 0 0 c6003 0 0 c7008 0 0 c8004 0 0 c900a 0 0 ca003 0 0
  //   cb023 0 0 cc003 0 0 cd003 0 0 ce003 0 0 cf003 0 0 1040 0 0 12450 0 0 33070 0 0 44070 0 0 54070 0 0
  //   66780 0 0 77300 0 0 108d01 0 0 a4228 0 0 f5106 0 0 f5166 0 0 115208 0 0 12f407 0 0 13e309 0 0 144603
  //   0 0 14ac03 0 0 153505 0 0 153505 0 0 166102 0 0 172404 0 0 0 166102 0 0 172404 0 0 193220 0 0 189220
  //   0 0 1a0087 0 0 1b0080 266*0 1b0080
endmodule

module ALU (
  input  [31:0] A,
  input  [31:0] B,
  input  [2:0] ALU_Operation,
  output ZF,
  output CF,
  output VF,
  output NF,
  output [31:0] ALU_Result
);

  wire full_adder32_1_cout, full_adder32_2_overflow;
  wire [31:0] and_1_out, full_adder32_1_out_6, full_adder32_2_out_6, nor_1_out, or_1_out;

  Multiplexer #(.select(3), .enable("false")) multiplexer_1 (
    .in0(full_adder32_1_cout), .in1(1'b0), .in2(1'b0), .in3(1'b0), .in4(1'b0), .in5(1'b0), .in6(1'b0),
    .in7(1'b0), .out(CF), .sel(ALU_Operation));
  Multiplexer #(.select(3), .enable("false")) multiplexer_2 (
    .in0(1'b0), .in1(full_adder32_2_overflow), .in2(1'b0), .in3(1'b0), .in4(1'b0), .in5(1'b0), .in6(1'b0),
    .in7(1'b0), .out(VF), .sel(ALU_Operation));
  Full_Adder32 full_adder32_1 (
    .A(A), .B(B), .in_3(1'b0), .out_6(full_adder32_1_out_6), .Cout(full_adder32_1_cout));  // open: Overflow
  Full_Adder32 full_adder32_2 (
    .A(A), .B(B), .in_3(1'b1), .out_6(full_adder32_2_out_6), .Overflow(full_adder32_2_overflow));  // open: Cout
  assign or_1_out = A | B;  // OR_Gate or_1, 32 bits wide
  assign nor_1_out = ~(A | B);  // NOR_Gate nor_1, 32 bits wide
  assign and_1_out = A & B;  // AND_Gate and_1, 32 bits wide
  Multiplexer #(.select(3), .width(32), .enable("false")) multiplexer_3 (
    .in0(full_adder32_1_out_6), .in1(full_adder32_2_out_6), .in2(or_1_out), .in3(nor_1_out), .in4(and_1_out),
    .in5({32{1'b0}}), .in6({32{1'b0}}), .in7({32{1'b0}}), .out(ALU_Result), .sel(ALU_Operation));
  nor nor_2 (ZF, ALU_Result[0], ALU_Result[1], ALU_Result[2], ALU_Result[3], ALU_Result[4], ALU_Result[5], ALU_Result[6], ALU_Result[7], ALU_Result[8], ALU_Result[9], ALU_Result[10], ALU_Result[11], ALU_Result[12], ALU_Result[13], ALU_Result[14], ALU_Result[15], ALU_Result[16], ALU_Result[17], ALU_Result[18], ALU_Result[19], ALU_Result[20], ALU_Result[21], ALU_Result[22], ALU_Result[23], ALU_Result[24], ALU_Result[25], ALU_Result[26], ALU_Result[27], ALU_Result[28], ALU_Result[29], ALU_Result[30], ALU_Result[31]);

  assign NF = ALU_Result[31];

  // Other names for the same wires on the sheet: ALUOP[2:0] = ALU_Operation
endmodule

module RFile (
  input  [4:0] RZ,
  input  [4:0] RY,
  input  [31:0] BusX,
  input  [4:0] RX,
  input  [4:0] Rp,
  input  [31:0] PC,
  input  Enable,
  input  CLK,
  output [31:0] Reg1,
  output [31:0] Reg4,
  output [31:0] Reg5,
  output [31:0] Reg2,
  output [31:0] Reg6,
  output [31:0] Reg3,
  output [31:0] BUSp,
  output [31:0] Reg7,
  output [31:0] Bus_Z,
  output [31:0] Reg8,
  output [31:0] Reg9,
  output [31:0] Reg10,
  output [31:0] Reg11,
  output [31:0] Bus_Y,
  output [31:0] Reg12,
  output [31:0] Reg13,
  output [31:0] Reg14,
  output [31:0] Reg15,
  output [31:0] Reg16,
  output [31:0] Reg17,
  output [31:0] Reg18,
  output [31:0] Reg19,
  output [31:0] Reg20,
  output [31:0] Reg21,
  output [31:0] Reg22,
  output [31:0] Reg23,
  output [31:0] Reg24,
  output [31:0] Reg25,
  output [31:0] Reg26,
  output [31:0] Reg27,
  output [31:0] Reg28,
  output [31:0] Reg29,
  output [31:0] Reg30,
  output [31:0] Reg31
);

  wire and_1_out, and_2_out, and_3_out, and_4_out, and_5_out, and_6_out, and_7_out, and_8_out, and_9_out,
       and_10_out, and_11_out, and_12_out, and_13_out, and_14_out, and_15_out, and_16_out, and_17_out,
       and_18_out, and_19_out, and_20_out, and_21_out, and_22_out, and_23_out, and_24_out, and_25_out,
       and_26_out, and_27_out, and_28_out, and_29_out, and_30_out, and_31_out, decoder_1_out0,
       decoder_2_out0, decoder_2_out1, decoder_2_out2, decoder_2_out3, decoder_2_out4, decoder_2_out5,
       decoder_2_out6, decoder_2_out7, decoder_2_out8, decoder_2_out9, decoder_2_out10, decoder_2_out11,
       decoder_2_out12, decoder_2_out13, decoder_2_out14, decoder_2_out15, decoder_2_out16, decoder_2_out17,
       decoder_2_out18, decoder_2_out19, decoder_2_out20, decoder_2_out21, decoder_2_out22, decoder_2_out23,
       decoder_2_out24, decoder_2_out25, decoder_2_out26, decoder_2_out27, decoder_2_out28, decoder_2_out29,
       decoder_2_out30, decoder_2_out31, decoder_3_out0, decoder_3_out1, decoder_3_out2, decoder_3_out3,
       decoder_3_out4, decoder_3_out5, decoder_3_out6, decoder_3_out7, decoder_3_out8, decoder_3_out9,
       decoder_3_out10, decoder_3_out11, decoder_3_out12, decoder_3_out13, decoder_3_out14, decoder_3_out15,
       decoder_3_out16, decoder_3_out17, decoder_3_out18, decoder_3_out19, decoder_3_out20, decoder_3_out21,
       decoder_3_out22, decoder_3_out23, decoder_3_out24, decoder_3_out25, decoder_3_out26, decoder_3_out27,
       decoder_3_out28, decoder_3_out29, decoder_3_out30, decoder_3_out31, R1, R2, R3, R4, R5, R6, R7, R8,
       R9, R10, R11, R12, R13, R14, R15, R16, R17, R18, R19, R20, R21, R22, R23, R24, R25, R26, R27, R28,
       R29, R30, R31;

  Decoder #(.select(5), .enable("false")) decoder_1 (
    .out0(decoder_1_out0), .out1(R1), .out2(R2), .out3(R3), .out4(R4), .out5(R5), .out6(R6), .out7(R7),
    .out8(R8), .out9(R9), .out10(R10), .out11(R11), .out12(R12), .out13(R13), .out14(R14), .out15(R15),
    .out16(R16), .out17(R17), .out18(R18), .out19(R19), .out20(R20), .out21(R21), .out22(R22), .out23(R23),
    .out24(R24), .out25(R25), .out26(R26), .out27(R27), .out28(R28), .out29(R29), .out30(R30), .out31(R31),
    .sel(RX));
  and and_1 (and_1_out, R2, Enable);
  and and_2 (and_2_out, R3, Enable);
  and and_3 (and_3_out, R4, Enable);
  and and_4 (and_4_out, R5, Enable);
  and and_5 (and_5_out, R6, Enable);
  and and_6 (and_6_out, R7, Enable);
  and and_7 (and_7_out, R8, Enable);
  and and_8 (and_8_out, R9, Enable);
  and and_9 (and_9_out, R10, Enable);
  and and_10 (and_10_out, R11, Enable);
  and and_11 (and_11_out, R12, Enable);
  and and_12 (and_12_out, R13, Enable);
  and and_13 (and_13_out, R14, Enable);
  and and_14 (and_14_out, R15, Enable);
  and and_15 (and_15_out, R16, Enable);
  and and_16 (and_16_out, R17, Enable);
  and and_17 (and_17_out, R18, Enable);
  and and_18 (and_18_out, R19, Enable);
  and and_19 (and_19_out, R20, Enable);
  and and_20 (and_20_out, R21, Enable);
  and and_21 (and_21_out, R22, Enable);
  and and_22 (and_22_out, R23, Enable);
  and and_23 (and_23_out, R24, Enable);
  and and_24 (and_24_out, R25, Enable);
  and and_25 (and_25_out, R26, Enable);
  and and_26 (and_26_out, R27, Enable);
  and and_27 (and_27_out, R28, Enable);
  and and_28 (and_28_out, R29, Enable);
  and and_29 (and_29_out, R30, Enable);
  and and_30 (and_30_out, R31, Enable);
  and and_31 (and_31_out, R1, Enable);
  Register #(.width(32)) u_r4 (.D(BusX), .en(and_3_out), .Q(Reg4), .clk(CLK));  // open: clr
  Register #(.width(32)) u_r6 (.D(BusX), .en(and_5_out), .Q(Reg6), .clk(CLK));  // open: clr
  Register #(.width(32)) u_r7 (.D(BusX), .en(and_6_out), .Q(Reg7), .clk(CLK));  // open: clr
  Register #(.width(32)) u_r8 (.D(BusX), .en(and_7_out), .Q(Reg8), .clk(CLK));  // open: clr
  Register #(.width(32)) u_r10 (.D(BusX), .en(and_9_out), .Q(Reg10), .clk(CLK));  // open: clr
  Register #(.width(32)) u_r11 (.D(BusX), .en(and_10_out), .Q(Reg11), .clk(CLK));  // open: clr
  Register #(.width(32)) u_r24 (.D(BusX), .en(and_23_out), .Q(Reg24), .clk(CLK));  // open: clr
  Register #(.width(32)) u_r25 (.D(BusX), .en(and_24_out), .Q(Reg25), .clk(CLK));  // open: clr
  Register #(.width(32)) u_r26 (.D(BusX), .en(and_25_out), .Q(Reg26), .clk(CLK));  // open: clr
  Register #(.width(32)) u_r27 (.D(BusX), .en(and_26_out), .Q(Reg27), .clk(CLK));  // open: clr
  Register #(.width(32)) u_r28 (.D(BusX), .en(and_27_out), .Q(Reg28), .clk(CLK));  // open: clr
  Register #(.width(32)) u_r29 (.D(BusX), .en(and_28_out), .Q(Reg29), .clk(CLK));  // open: clr
  Register #(.width(32)) u_r30 (.D(BusX), .en(and_29_out), .Q(Reg30), .clk(CLK));  // open: clr
  Register #(.width(32)) u_r31 (.D(BusX), .en(and_30_out), .Q(Reg31), .clk(CLK));  // open: clr
  Register #(.width(32)) u_r1 (.D(BusX), .en(and_31_out), .Q(Reg1), .clk(CLK));  // open: clr
  Register #(.width(32)) u_r2 (.D(BusX), .en(and_1_out), .Q(Reg2), .clk(CLK));  // open: clr
  Register #(.width(32)) u_r3 (.D(BusX), .en(and_2_out), .Q(Reg3), .clk(CLK));  // open: clr
  Register #(.width(32)) u_r5 (.D(BusX), .en(and_4_out), .Q(Reg5), .clk(CLK));  // open: clr
  Register #(.width(32)) u_r9 (.D(BusX), .en(and_8_out), .Q(Reg9), .clk(CLK));  // open: clr
  Register #(.width(32)) u_r12 (.D(BusX), .en(and_11_out), .Q(Reg12), .clk(CLK));  // open: clr
  Register #(.width(32)) u_r13 (.D(BusX), .en(and_12_out), .Q(Reg13), .clk(CLK));  // open: clr
  Register #(.width(32)) u_r14 (.D(BusX), .en(and_13_out), .Q(Reg14), .clk(CLK));  // open: clr
  Register #(.width(32)) u_r15 (.D(BusX), .en(and_14_out), .Q(Reg15), .clk(CLK));  // open: clr
  Register #(.width(32)) u_r16 (.D(BusX), .en(and_15_out), .Q(Reg16), .clk(CLK));  // open: clr
  Register #(.width(32)) u_r17 (.D(BusX), .en(and_16_out), .Q(Reg17), .clk(CLK));  // open: clr
  Register #(.width(32)) u_r18 (.D(BusX), .en(and_17_out), .Q(Reg18), .clk(CLK));  // open: clr
  Register #(.width(32)) u_r19 (.D(BusX), .en(and_18_out), .Q(Reg19), .clk(CLK));  // open: clr
  Register #(.width(32)) u_r20 (.D(BusX), .en(and_19_out), .Q(Reg20), .clk(CLK));  // open: clr
  Register #(.width(32)) u_r21 (.D(BusX), .en(and_20_out), .Q(Reg21), .clk(CLK));  // open: clr
  Register #(.width(32)) u_r22 (.D(BusX), .en(and_21_out), .Q(Reg22), .clk(CLK));  // open: clr
  Register #(.width(32)) u_r23 (.D(BusX), .en(and_22_out), .Q(Reg23), .clk(CLK));  // open: clr
  assign Bus_Y = decoder_2_out3 ? Reg3 : 32'bz;  // Controlled_Buffer controlled_buffer_1
  assign Bus_Y = decoder_2_out0 ? {32{1'b0}} : 32'bz;  // Controlled_Buffer controlled_buffer_2
  assign Bus_Y = decoder_2_out1 ? Reg1 : 32'bz;  // Controlled_Buffer controlled_buffer_3
  assign Bus_Y = decoder_2_out2 ? Reg2 : 32'bz;  // Controlled_Buffer controlled_buffer_4
  assign Bus_Y = decoder_2_out4 ? Reg4 : 32'bz;  // Controlled_Buffer controlled_buffer_5
  Decoder #(.select(5), .enable("false")) decoder_2 (
    .out0(decoder_2_out0), .out1(decoder_2_out1), .out2(decoder_2_out2), .out3(decoder_2_out3),
    .out4(decoder_2_out4), .out5(decoder_2_out5), .out6(decoder_2_out6), .out7(decoder_2_out7),
    .out8(decoder_2_out8), .out9(decoder_2_out9), .out10(decoder_2_out10), .out11(decoder_2_out11),
    .out12(decoder_2_out12), .out13(decoder_2_out13), .out14(decoder_2_out14), .out15(decoder_2_out15),
    .out16(decoder_2_out16), .out17(decoder_2_out17), .out18(decoder_2_out18), .out19(decoder_2_out19),
    .out20(decoder_2_out20), .out21(decoder_2_out21), .out22(decoder_2_out22), .out23(decoder_2_out23),
    .out24(decoder_2_out24), .out25(decoder_2_out25), .out26(decoder_2_out26), .out27(decoder_2_out27),
    .out28(decoder_2_out28), .out29(decoder_2_out29), .out30(decoder_2_out30), .out31(decoder_2_out31),
    .sel(RY));
  assign Bus_Y = decoder_2_out5 ? Reg5 : 32'bz;  // Controlled_Buffer controlled_buffer_6
  assign Bus_Y = decoder_2_out6 ? Reg6 : 32'bz;  // Controlled_Buffer controlled_buffer_7
  assign Bus_Y = decoder_2_out7 ? Reg7 : 32'bz;  // Controlled_Buffer controlled_buffer_8
  assign Bus_Y = decoder_2_out8 ? Reg8 : 32'bz;  // Controlled_Buffer controlled_buffer_9
  assign Bus_Y = decoder_2_out9 ? Reg9 : 32'bz;  // Controlled_Buffer controlled_buffer_10
  assign Bus_Y = decoder_2_out10 ? Reg10 : 32'bz;  // Controlled_Buffer controlled_buffer_11
  assign Bus_Y = decoder_2_out11 ? Reg11 : 32'bz;  // Controlled_Buffer controlled_buffer_12
  assign Bus_Y = decoder_2_out12 ? Reg12 : 32'bz;  // Controlled_Buffer controlled_buffer_13
  assign Bus_Y = decoder_2_out13 ? Reg13 : 32'bz;  // Controlled_Buffer controlled_buffer_14
  assign Bus_Y = decoder_2_out14 ? Reg14 : 32'bz;  // Controlled_Buffer controlled_buffer_15
  assign Bus_Y = decoder_2_out15 ? Reg15 : 32'bz;  // Controlled_Buffer controlled_buffer_16
  assign Bus_Y = decoder_2_out16 ? Reg16 : 32'bz;  // Controlled_Buffer controlled_buffer_17
  assign Bus_Y = decoder_2_out17 ? Reg17 : 32'bz;  // Controlled_Buffer controlled_buffer_18
  assign Bus_Y = decoder_2_out18 ? Reg18 : 32'bz;  // Controlled_Buffer controlled_buffer_19
  assign Bus_Y = decoder_2_out19 ? Reg19 : 32'bz;  // Controlled_Buffer controlled_buffer_20
  assign Bus_Y = decoder_2_out20 ? Reg20 : 32'bz;  // Controlled_Buffer controlled_buffer_21
  assign Bus_Y = decoder_2_out21 ? Reg21 : 32'bz;  // Controlled_Buffer controlled_buffer_22
  assign Bus_Y = decoder_2_out22 ? Reg22 : 32'bz;  // Controlled_Buffer controlled_buffer_23
  assign Bus_Y = decoder_2_out23 ? Reg23 : 32'bz;  // Controlled_Buffer controlled_buffer_24
  assign Bus_Y = decoder_2_out24 ? Reg24 : 32'bz;  // Controlled_Buffer controlled_buffer_25
  assign Bus_Y = decoder_2_out25 ? Reg25 : 32'bz;  // Controlled_Buffer controlled_buffer_26
  assign Bus_Y = decoder_2_out26 ? Reg26 : 32'bz;  // Controlled_Buffer controlled_buffer_27
  assign Bus_Y = decoder_2_out27 ? Reg27 : 32'bz;  // Controlled_Buffer controlled_buffer_28
  assign Bus_Y = decoder_2_out28 ? Reg28 : 32'bz;  // Controlled_Buffer controlled_buffer_29
  assign Bus_Y = decoder_2_out29 ? Reg29 : 32'bz;  // Controlled_Buffer controlled_buffer_30
  assign Bus_Y = decoder_2_out30 ? Reg30 : 32'bz;  // Controlled_Buffer controlled_buffer_31
  assign Bus_Y = decoder_2_out31 ? Reg31 : 32'bz;  // Controlled_Buffer controlled_buffer_32
  assign Bus_Z = decoder_3_out0 ? {32{1'b0}} : 32'bz;  // Controlled_Buffer controlled_buffer_33
  assign Bus_Z = decoder_3_out1 ? Reg1 : 32'bz;  // Controlled_Buffer controlled_buffer_34
  assign Bus_Z = decoder_3_out2 ? Reg2 : 32'bz;  // Controlled_Buffer controlled_buffer_35
  assign Bus_Z = decoder_3_out3 ? Reg3 : 32'bz;  // Controlled_Buffer controlled_buffer_36
  assign Bus_Z = decoder_3_out4 ? Reg4 : 32'bz;  // Controlled_Buffer controlled_buffer_37
  assign Bus_Z = decoder_3_out5 ? Reg5 : 32'bz;  // Controlled_Buffer controlled_buffer_38
  assign Bus_Z = decoder_3_out6 ? Reg6 : 32'bz;  // Controlled_Buffer controlled_buffer_39
  assign Bus_Z = decoder_3_out7 ? Reg7 : 32'bz;  // Controlled_Buffer controlled_buffer_40
  assign Bus_Z = decoder_3_out8 ? Reg8 : 32'bz;  // Controlled_Buffer controlled_buffer_41
  assign Bus_Z = decoder_3_out9 ? Reg9 : 32'bz;  // Controlled_Buffer controlled_buffer_42
  assign Bus_Z = decoder_3_out10 ? Reg10 : 32'bz;  // Controlled_Buffer controlled_buffer_43
  assign Bus_Z = decoder_3_out11 ? Reg11 : 32'bz;  // Controlled_Buffer controlled_buffer_44
  assign Bus_Z = decoder_3_out12 ? Reg12 : 32'bz;  // Controlled_Buffer controlled_buffer_45
  assign Bus_Z = decoder_3_out13 ? Reg13 : 32'bz;  // Controlled_Buffer controlled_buffer_46
  assign Bus_Z = decoder_3_out14 ? Reg14 : 32'bz;  // Controlled_Buffer controlled_buffer_47
  assign Bus_Z = decoder_3_out15 ? Reg15 : 32'bz;  // Controlled_Buffer controlled_buffer_48
  assign Bus_Z = decoder_3_out16 ? Reg16 : 32'bz;  // Controlled_Buffer controlled_buffer_49
  assign Bus_Z = decoder_3_out17 ? Reg17 : 32'bz;  // Controlled_Buffer controlled_buffer_50
  assign Bus_Z = decoder_3_out18 ? Reg18 : 32'bz;  // Controlled_Buffer controlled_buffer_51
  assign Bus_Z = decoder_3_out19 ? Reg19 : 32'bz;  // Controlled_Buffer controlled_buffer_52
  assign Bus_Z = decoder_3_out20 ? Reg20 : 32'bz;  // Controlled_Buffer controlled_buffer_53
  assign Bus_Z = decoder_3_out21 ? Reg21 : 32'bz;  // Controlled_Buffer controlled_buffer_54
  assign Bus_Z = decoder_3_out22 ? Reg22 : 32'bz;  // Controlled_Buffer controlled_buffer_55
  assign Bus_Z = decoder_3_out23 ? Reg23 : 32'bz;  // Controlled_Buffer controlled_buffer_56
  assign Bus_Z = decoder_3_out24 ? Reg24 : 32'bz;  // Controlled_Buffer controlled_buffer_57
  assign Bus_Z = decoder_3_out25 ? Reg25 : 32'bz;  // Controlled_Buffer controlled_buffer_58
  assign Bus_Z = decoder_3_out26 ? Reg26 : 32'bz;  // Controlled_Buffer controlled_buffer_59
  assign Bus_Z = decoder_3_out27 ? Reg27 : 32'bz;  // Controlled_Buffer controlled_buffer_60
  assign Bus_Z = decoder_3_out28 ? Reg28 : 32'bz;  // Controlled_Buffer controlled_buffer_61
  assign Bus_Z = decoder_3_out29 ? Reg29 : 32'bz;  // Controlled_Buffer controlled_buffer_62
  assign Bus_Z = decoder_3_out30 ? Reg30 : 32'bz;  // Controlled_Buffer controlled_buffer_63
  assign Bus_Z = decoder_3_out31 ? Reg31 : 32'bz;  // Controlled_Buffer controlled_buffer_64
  Decoder #(.select(5), .enable("false")) decoder_3 (
    .out0(decoder_3_out0), .out1(decoder_3_out1), .out2(decoder_3_out2), .out3(decoder_3_out3),
    .out4(decoder_3_out4), .out5(decoder_3_out5), .out6(decoder_3_out6), .out7(decoder_3_out7),
    .out8(decoder_3_out8), .out9(decoder_3_out9), .out10(decoder_3_out10), .out11(decoder_3_out11),
    .out12(decoder_3_out12), .out13(decoder_3_out13), .out14(decoder_3_out14), .out15(decoder_3_out15),
    .out16(decoder_3_out16), .out17(decoder_3_out17), .out18(decoder_3_out18), .out19(decoder_3_out19),
    .out20(decoder_3_out20), .out21(decoder_3_out21), .out22(decoder_3_out22), .out23(decoder_3_out23),
    .out24(decoder_3_out24), .out25(decoder_3_out25), .out26(decoder_3_out26), .out27(decoder_3_out27),
    .out28(decoder_3_out28), .out29(decoder_3_out29), .out30(decoder_3_out30), .out31(decoder_3_out31),
    .sel(RZ));
  // also tied to GND on the sheet: decoder_1_out0

  // Other names for the same wires on the sheet: data[31:0] = BusX
endmodule

module Full_Adder_8bit (
  input  [7:0] A,
  input  [7:0] B,
  input  Cin,
  output Cout,
  output [7:0] Sub
);

  wire full_adder_2_cout;

  // Probe on A
  // Probe on B
  Full_Adder full_adder_1 (.A(A[7:4]), .B(B[7:4]), .Cout(Cout), .Cin(full_adder_2_cout), .Sub(Sub[7:4]));
  // Probe on Sub
  Full_Adder full_adder_2 (.A(A[3:0]), .B(B[3:0]), .Cout(full_adder_2_cout), .Cin(Cin), .Sub(Sub[3:0]));

  // Other names for the same wires on the sheet: A_0_3[3:0] = A[3:0]; A_4_7[3:0] = A[7:4]; B_0_3[3:0] = B[3:0];
  //   B_4_7[3:0] = B[7:4]
endmodule

module Full_Adder32 (
  input  [31:0] A,
  input  [31:0] B,
  input  in_3,
  output Cout,
  output Overflow,
  output [31:0] out_6
);

  wire full_adder_8bit_2_cout, full_adder_8bit_3_cout, full_adder_8bit_4_cout;

  xor xor_1 (Overflow, Cout, full_adder_8bit_2_cout);
  // Probe on A
  // Probe on B
  Full_Adder_8bit full_adder_8bit_1 (
    .A(B[31:24]), .B(A[31:24]), .Cout(Cout), .Sub(out_6[31:24]), .Cin(full_adder_8bit_2_cout));
  Full_Adder_8bit full_adder_8bit_2 (
    .A(B[23:16]), .B(A[23:16]), .Cout(full_adder_8bit_2_cout), .Sub(out_6[23:16]),
    .Cin(full_adder_8bit_3_cout));
  Full_Adder_8bit full_adder_8bit_3 (
    .A(B[15:8]), .B(A[15:8]), .Cout(full_adder_8bit_3_cout), .Sub(out_6[15:8]), .Cin(full_adder_8bit_4_cout));
  // Probe on out_6
  Full_Adder_8bit full_adder_8bit_4 (
    .A(B[7:0]), .B(A[7:0]), .Cout(full_adder_8bit_4_cout), .Sub(out_6[7:0]), .Cin(in_3));
endmodule

module Control_Unit (
  input  [4:0] Op_Code,
  output [2:0] ALUOP,
  output [1:0] PCSel,
  output RegDes,
  output ExtOp,
  output ALUSrc,
  output WE,
  output MemWrite,
  output MemRead,
  output [1:0] WBdata
);

  wire [31:13] rom_1_data;

  ROM #(.addrWidth(5), .dataWidth(32)) rom_1 (
    .addr(Op_Code), .data({rom_1_data, WBdata, MemRead, MemWrite, WE, ALUSrc, ExtOp, RegDes, PCSel, ALUOP}));  // open: sel

  // Notes on the sheet:
  //   contents of rom_1 (hex, n*v repeats v):
  //   100 101 102 103 104 10 160 182 183 184 d60 260 8 1128
endmodule

module PC_Control (
  input  [1:0] PC_Selection,
  input  [19:0] PC,
  input  [19:0] NPC,
  input  [21:0] OFFSET,
  input  [19:0] Reg,
  output [19:0] NextPC
);

  wire [19:0] bit_extender_1_out, JumpTarget, PC___1;

  Bit_Extender #(.in_width(22), .out_width(20), .\type ("sign")) bit_extender_1 (.in(OFFSET), .out(bit_extender_1_out));
  Adder #(.width(20)) adder_1 (.a(PC), .b(20'h1), .out(PC___1), .cin(1'b0));  // open: cout
  Multiplexer #(.select(2), .width(20), .enable("false")) multiplexer_1 (
    .in0(PC___1), .in1(JumpTarget), .in2(Reg), .in3({20{1'b0}}), .out(NextPC), .sel(PC_Selection));
  Adder #(.width(20)) adder_2 (.a(NPC), .b(bit_extender_1_out), .out(JumpTarget), .cin(1'b0));  // open: cout

  // Other names for the same wires on the sheet: JREG[19:0] = Reg
endmodule

module ID_EX (
  input  [31:0] SOURCE1,
  input  [31:0] in_2,
  input  [31:0] SOURCE2,
  input  [31:0] in_4,
  input  [31:0] IMM,
  input  [31:0] in_6,
  input  [31:0] PC_1,
  input  [31:0] in_8,
  input  [2:0] ALUOP,
  input  ALUSrc,
  input  [4:0] DESTENATION,
  input  [4:0] in_12,
  input  MEMW,
  input  MEMR,
  input  Regwrite,
  input  in_16,
  input  [1:0] WB,
  input  in_18,
  output [2:0] out_19,
  output out_20,
  output out_21,
  output out_22,
  output [1:0] out_23
);

  Register #(.width(32)) register_1 (.D(SOURCE1), .en(1'b1), .Q(in_2), .clk(in_18));  // open: clr
  Register #(.width(32)) register_2 (.D(SOURCE2), .en(1'b1), .Q(in_4), .clk(in_18));  // open: clr
  Register #(.width(32)) register_3 (.D(IMM), .en(1'b1), .Q(in_6), .clk(in_18));  // open: clr
  Register #(.width(32)) register_4 (.D(PC_1), .en(1'b1), .Q(in_8), .clk(in_18));  // open: clr
  Register #(.width(3)) register_5 (.D(ALUOP), .en(1'b1), .Q(out_19), .clk(in_18));  // open: clr
  Register #(.width(1)) register_6 (.D(ALUSrc), .en(1'b1), .Q(out_20), .clk(in_18));  // open: clr
  Register #(.width(5)) register_7 (.D(DESTENATION), .en(1'b1), .Q(in_12), .clk(in_18));  // open: clr
  Register #(.width(1)) register_8 (.D(MEMW), .en(1'b1), .Q(out_21), .clk(in_18));  // open: clr
  Register #(.width(1)) register_9 (.D(MEMR), .en(1'b1), .Q(out_22), .clk(in_18));  // open: clr
  Register #(.width(1)) register_10 (.D(Regwrite), .en(1'b1), .Q(in_16), .clk(in_18));  // open: clr
  Register #(.width(2)) register_11 (.D(WB), .en(1'b1), .Q(out_23), .clk(in_18));  // open: clr

  // Other names for the same wires on the sheet: CLK = in_18
endmodule

module Forwarding_Unit (
  input  [4:0] RS1,
  input  [4:0] RD1,
  input  WE_EX,
  input  [4:0] RD2,
  input  MemRead_MEM,
  input  [4:0] RD3,
  input  WE_WB,
  input  [4:0] RS2,
  input  [4:0] RP,
  output [1:0] FA,
  output [1:0] FB,
  output [1:0] FP
);

  wire and_1_out, and_2_out, and_3_out, and_4_out, and_5_out, and_6_out, and_7_out, and_8_out, and_9_out,
       and_10_out, and_11_out, and_12_out, and_13_out, and_14_out, and_15_out, and_16_out, and_17_out,
       and_18_out, comparator_1_eq, comparator_2_eq, comparator_3_eq, comparator_4_eq, comparator_5_eq,
       comparator_6_eq, comparator_7_eq, comparator_8_eq, comparator_9_eq, not_1_out, not_2_out, not_3_out,
       not_4_out, not_5_out, not_6_out, not_7_out, not_8_out, not_9_out, or_1_out, or_2_out, or_3_out,
       or_4_out, or_5_out, or_6_out, or_7_out, or_8_out, or_9_out;
  wire [4:0] RD2_t;

  or or_1 (or_1_out, RS1[0], RS1[1], RS1[2], RS1[3], RS1[4]);
  or or_2 (or_2_out, RP[0], RP[1], RP[2], RP[3], RP[4]);
  or or_3 (or_3_out, RP[0], RP[1], RP[2], RP[3], RP[4]);
  or or_4 (or_4_out, RP[0], RP[1], RP[2], RP[3], RP[4]);
  or or_5 (or_5_out, RS1[0], RS1[1], RS1[2], RS1[3], RS1[4]);
  Comparator #(.width(5)) comparator_1 (.a(RS1), .b(RD1), .eq(comparator_1_eq));  // open: gt, lt
  or or_6 (or_6_out, RS1[0], RS1[1], RS1[2], RS1[3], RS1[4]);
  Comparator #(.width(5)) comparator_2 (.a(RS1), .b(RD2), .eq(comparator_2_eq));  // open: gt, lt
  Comparator #(.width(5)) comparator_3 (.a(RS1), .b(RD2), .eq(comparator_3_eq));  // open: gt, lt
  or or_7 (or_7_out, RS2[0], RS2[1], RS2[2], RS2[3], RS2[4]);
  or or_8 (or_8_out, RS2[0], RS2[1], RS2[2], RS2[3], RS2[4]);
  Comparator #(.width(5)) comparator_4 (.a(RS2), .b(RD2_t), .eq(comparator_4_eq));  // open: gt, lt
  or or_9 (or_9_out, RS2[0], RS2[1], RS2[2], RS2[3], RS2[4]);
  Comparator #(.width(5)) comparator_5 (.a(RS2), .b(RD2), .eq(comparator_5_eq));  // open: gt, lt
  Comparator #(.width(5)) comparator_6 (.a(RP), .b(RD1), .eq(comparator_6_eq));  // open: gt, lt
  Comparator #(.width(5)) comparator_7 (.a(RP), .b(RD2_t), .eq(comparator_7_eq));  // open: gt, lt
  Comparator #(.width(5)) comparator_8 (.a(RP), .b(RD2), .eq(comparator_8_eq));  // open: gt, lt
  Comparator #(.width(5)) comparator_9 (.a(RS2), .b(RD1), .eq(comparator_9_eq));  // open: gt, lt
  and and_1 (and_1_out, or_5_out, comparator_1_eq, WE_EX);
  and and_2 (and_2_out, or_6_out, comparator_2_eq, MemRead_MEM);
  and and_3 (and_3_out, or_1_out, comparator_3_eq, WE_WB);
  and and_4 (and_4_out, or_7_out, comparator_9_eq, WE_EX);
  and and_5 (and_5_out, or_8_out, comparator_4_eq, MemRead_MEM);
  and and_6 (and_6_out, or_9_out, comparator_5_eq, WE_WB);
  and and_7 (and_7_out, or_2_out, comparator_6_eq, WE_EX);
  and and_8 (and_8_out, or_3_out, comparator_7_eq, MemRead_MEM);
  and and_9 (and_9_out, or_4_out, comparator_8_eq, WE_WB);
  not not_1 (not_1_out, and_7_out);
  not not_2 (not_2_out, and_8_out);
  not not_3 (not_3_out, and_1_out);
  not not_4 (not_4_out, and_1_out);
  not not_5 (not_5_out, and_2_out);
  not not_6 (not_6_out, and_4_out);
  not not_7 (not_7_out, and_4_out);
  not not_8 (not_8_out, and_5_out);
  not not_9 (not_9_out, and_7_out);
  and and_10 (and_10_out, not_9_out, and_8_out);
  and and_11 (and_11_out, not_2_out, and_9_out);
  and and_12 (and_12_out, not_3_out, and_3_out);
  and and_13 (and_13_out, not_4_out, and_2_out);
  and and_14 (and_14_out, not_5_out, and_3_out);
  and and_15 (and_15_out, not_6_out, and_6_out);
  and and_16 (and_16_out, not_7_out, and_5_out);
  and and_17 (and_17_out, not_8_out, and_6_out);
  and and_18 (and_18_out, not_1_out, and_9_out);
  or or_10 (FA[1], and_12_out, and_13_out);
  or or_11 (FA[0], and_14_out, and_1_out);
  or or_12 (FB[1], and_15_out, and_16_out);
  or or_13 (FB[0], and_17_out, and_4_out);
  or or_14 (FP[1], and_18_out, and_10_out);
  or or_15 (FP[0], and_11_out, and_7_out);

  assign RD3 = RD2;

  // Notes on the sheet:
  //   A1
  //   A2
  //   A3
  //   A3
  //   A1
  //   A2
  //   A3
  //   A1
  //   A2
endmodule

module EX_MEM (
  input  [31:0] ALU_RES,
  input  [31:0] SOURCE2,
  input  [31:0] in_3,
  input  [31:0] PC_1,
  input  [31:0] in_5,
  input  [4:0] DESTENATION,
  input  [4:0] in_7,
  input  Regwrite,
  input  in_9,
  input  MemRd,
  input  in_11,
  input  MemWr,
  input  in_13,
  input  [1:0] WB_DATA,
  input  [1:0] in_15,
  input  in_16,
  output [31:0] out_17
);

  Register #(.width(32)) register_1 (.D(ALU_RES), .en(1'b1), .Q(out_17), .clk(in_16));  // open: clr
  Register #(.width(32)) register_2 (.D(SOURCE2), .en(1'b1), .Q(in_3), .clk(in_16));  // open: clr
  Register #(.width(32)) register_3 (.D(PC_1), .en(1'b1), .Q(in_5), .clk(in_16));  // open: clr
  Register #(.width(5)) register_4 (.D(DESTENATION), .en(1'b1), .Q(in_7), .clk(in_16));  // open: clr
  Register #(.width(1)) register_5 (.D(Regwrite), .en(1'b1), .Q(in_9), .clk(in_16));  // open: clr
  Register #(.width(1)) register_6 (.D(MemRd), .en(1'b1), .Q(in_11), .clk(in_16));  // open: clr
  Register #(.width(1)) register_7 (.D(MemWr), .en(1'b1), .Q(in_13), .clk(in_16));  // open: clr
  Register #(.width(2)) register_8 (.D(WB_DATA), .en(1'b1), .Q(in_15), .clk(in_16));  // open: clr

  // Other names for the same wires on the sheet: CLK = in_16
endmodule

module MEM_WB (
  input  [31:0] DATA,
  input  [31:0] in_2,
  input  [4:0] DESTENATION,
  input  [4:0] in_4,
  input  Regwrite,
  input  in_6,
  input  in_7
);

  Register #(.width(32)) register_1 (.D(DATA), .en(1'b1), .Q(in_2), .clk(in_7));  // open: clr
  Register #(.width(5)) register_2 (.D(DESTENATION), .en(1'b1), .Q(in_4), .clk(in_7));  // open: clr
  Register #(.width(1)) register_3 (.D(Regwrite), .en(1'b1), .Q(in_6), .clk(in_7));  // open: clr

  // Other names for the same wires on the sheet: CLK = in_7
endmodule

module Bubble (
  input  EX_MEM_READ,
  input  [1:0] FA,
  input  [1:0] FB,
  output Stall
);

  wire and_1_out, and_2_out, not_1_out, not_2_out;

  not not_1 (not_1_out, FB[1]);
  not not_2 (not_2_out, FA[1]);
  and and_1 (and_1_out, EX_MEM_READ, not_1_out, FB[0]);
  and and_2 (and_2_out, EX_MEM_READ, not_2_out, FA[0]);
  or or_1 (Stall, and_1_out, and_2_out);
endmodule

module Extender (
  input  [11:0] Imm,
  input  EXTSignal,
  output [31:0] ImmExtender
);

  wire [31:0] bit_extender_1_out, bit_extender_2_out;

  assign bit_extender_1_out = {{20{1'b0}}, Imm};  // Bit_Extender bit_extender_1
  assign bit_extender_2_out = {{20{Imm[11]}}, Imm};  // Bit_Extender bit_extender_2
  Multiplexer #(.width(32), .enable("false")) multiplexer_1 (
    .in0(bit_extender_1_out), .in1(bit_extender_2_out), .out(ImmExtender), .sel(EXTSignal));
endmodule

module Hazarad_Detection (
  input  MEMR,
  input  [1:0] FA,
  input  [1:0] FB,
  input  [1:0] FP,
  input  [4:0] OPCode,
  output Stall,
  output Kill
);

  Stall_Detection stall_detection_1 (.MEMRead(MEMR), .FowordA(FA), .FowordB(FB), .FowordP(FP), .Stall(Stall));
  Kill_Detection kill_detection_1 (.OPCode(OPCode), .Kill(Kill));
endmodule

module Stall_Detection (
  input  MEMRead,
  input  [1:0] FowordA,
  input  [1:0] FowordB,
  input  [1:0] FowordP,
  output Stall
);

  wire comparator_1_eq, comparator_2_eq, comparator_3_eq, or_1_out;

  Comparator #(.width(2)) comparator_1 (.a(2'b10), .b(FowordA), .eq(comparator_1_eq));  // open: gt, lt
  Comparator #(.width(2)) comparator_2 (.a(2'b10), .b(FowordB), .eq(comparator_2_eq));  // open: gt, lt
  Comparator #(.width(2)) comparator_3 (.a(2'b10), .b(FowordP), .eq(comparator_3_eq));  // open: gt, lt
  or or_1 (or_1_out, comparator_1_eq, comparator_2_eq, comparator_3_eq);
  and and_1 (Stall, MEMRead, or_1_out);
endmodule

module Kill_Detection (
  input  [4:0] OPCode,
  output Kill
);

  wire comparator_1_eq, comparator_2_eq, comparator_3_eq;

  Comparator #(.width(5)) comparator_1 (.a(OPCode), .b(5'b01011), .eq(comparator_1_eq));  // open: gt, lt
  Comparator #(.width(5)) comparator_2 (.a(OPCode), .b(5'b01100), .eq(comparator_2_eq));  // open: gt, lt
  Comparator #(.width(5)) comparator_3 (.a(OPCode), .b(5'b01101), .eq(comparator_3_eq));  // open: gt, lt
  or or_1 (Kill, comparator_1_eq, comparator_2_eq, comparator_3_eq);
endmodule

module IF_ID (
  input  [31:0] Instruction,
  input  [31:0] PC,
  input  clk,
  output [31:0] out_4,
  output [31:0] out_5
);

  Register #(.width(32)) register_1 (.D(Instruction), .en(1'b1), .Q(out_4), .clk(clk));  // open: clr
  Register #(.width(32)) register_2 (.D(PC), .en(1'b1), .Q(out_5), .clk(clk));  // open: clr
endmodule
